# Fritzing sketch Lora (saved by Fritzing 0.9.6b)
circuit board: 10.3767cm x 6.15032cm
breadboards: 1

parts:
  U1 = ESP8266 WiFi Module [part_number=ESP8266]
  Componente1 = Arduino Uno (Rev3) - ICSP
  Componente2 = Arduino Nano (Rev3.0)

nets (from the breadboard view):
  N1: U1.RXD, Componente1.D10_PWM/SS
  N2: U1.GPIO_2, Componente1.D13/SCK
  N3: U1.CH_PD, U1.ADC_0, Componente1.GND
  N4: U1.GPIO_4, Componente1.D12/MISO
  N5: U1.GPIO_5, Componente1.D11_PWM/MOSI
  N6: U1.GPIO_16, Componente1.3V3, Componente2.D1/TX
  N7: U1.GPIO_14, Componente1.D9_PWM
  N8: U1.GPIO_12, Componente1.D2

// code stored in the sketch: Transmiter.ino
#include <SPI.h>
#include <LoRa.h> 

void setup() {
  Serial.begin(9600);
  pinMode(4, OUTPUT);
  
  while (!Serial);  
  Serial.println("LoRa Sender");
  if (!LoRa.begin(433E6)) { // or 915E6, the MHz speed of yout module
    Serial.println("Starting LoRa failed!");
    while (1);
  }else{
    digitalWrite(4, HIGH);
  }
}
 
void loop() {
  String val = "Holora";
  LoRa.beginPacket();  
  LoRa.print(val);
  LoRa.endPacket();
  Serial.println(val + " Estoy en Loop");

  digitalWrite(4, HIGH);   // turn the LED on (HIGH is the voltage level)
  delay(50);                       // wait for a second
  digitalWrite(4, LOW);    // turn the LED off by making the voltage LOW
  delay(50);                       // wait for a second

}
