# Fritzing sketch Planta Feliz 2 (saved by Fritzing 0.9.6b)
breadboards: 1

parts:
  Componente1 = Soil Moisture Sensor
  U2 = SHT1x Humdity Sensor [package=sht1x]
  Componente2 = NRF24L01+ Breakout Board
  LCD1 = LCD screen  # not connected
  S1 = Momentary Switch [package=ksa_sealed_tac_switch]
  S2 = Momentary Switch [package=ksa_sealed_tac_switch]
  U3 = POT_SWITCH [package=pot_pth_switch]
  R1 = PHOTOCELL [package=photocell-kit]
  Componente3 = Arduino Nano (Rev3.0) (ICSP)  # not connected

nets:
  VCC: Componente1.VCC, U2.VDD, Componente2.VCC, U3.G$1_A
  GND: Componente1.GND, U2.GND, Componente2.GND, S1.4, S2.4, U3.G$2_2, R1.P$2
